# Fritzing sketch Lab_10 (saved by Fritzing 0.9.3b)
circuit board: 8.46667cm x 5.64444cm
breadboards: 1

parts:
  ESP32-PICO-KIT_v4 = ESP32-PICO-KIT_v4 [part_number=1904-1030-ND chip_label=ESP32-PICO-KIT_V4 package="DIP (Dual Inline) [THT]"]
  LED1 = LED - 3mm [color="Red (633nm)" package="3 mm [THT]"]
  R1 = Resistor [tolerance=±5% resistance=220 package=THT]

nets:
  N1: ESP32-PICO-KIT_v4.GND#18, R1.Pin_0
  N2: ESP32-PICO-KIT_v4.IO21, LED1.anode
  N3: LED1.cathode, R1.Pin_1
